# Fritzing sketch Fritzing (saved by Fritzing 0.7.7b)
breadboards: 4

parts:
  U1 = atmega168 [package=dip]
  S1 = Pushbutton [package="[THT]"]
  S2 = Pushbutton [package="[THT]"]
  S3 = Pushbutton [package="[THT]"]
  S4 = Pushbutton [package="[THT]"]
  S5 = Pushbutton [package="[THT]"]
  S6 = Pushbutton [package="[THT]"]
  S7 = Pushbutton [package="[THT]"]
  S8 = Pushbutton [package="[THT]"]
  S9 = Pushbutton [package="[THT]"]
  S10 = Pushbutton [package="[THT]"]
  S11 = Pushbutton [package="[THT]"]
  IC1 = IC, DIP package, 16 pins [chip_label=IC]  # not connected
  XTAL1 = Crystal [frequency="16 Mhz" package=THT]
  S12 = Pushbutton [package="[THT]"]
  S13 = Pushbutton [package="[THT]"]
  S14 = Pushbutton [package="[THT]"]
  S15 = Pushbutton [package="[THT]"]
  Arduino1 = Arduino
  U2 = atmega168 [package=dip]
  U3 = Voltage Regulator - 3.3V [package="TO220 [THT]"]  # not connected
  S16 = Pushbutton [package="[THT]"]
  M1 = DC Motor  # not connected
  M2 = DC Motor  # not connected
  Part1 = IMU Digital Combo Board 6DOF

nets:
  N1: U1.D7, Arduino1.SDA, U2.A4, Part1.SDA
  N2: U1.D8, Arduino1.SCL, U2.A5, Part1.SCL
  N3: U1.A0, XTAL1.pin_1
  N4: U1.A1, XTAL1.pin_0
  N5: S1.Pin_1, S1.Pin_2
  N6: S1.Pin_3, S1.Pin_4
  N7: S2.Pin_1, S2.Pin_2
  N8: S2.Pin_3, S2.Pin_4
  N9: S3.Pin_1, S3.Pin_2
  N10: S3.Pin_3, S3.Pin_4
  N11: S4.Pin_1, S4.Pin_2
  N12: S4.Pin_3, S4.Pin_4
  N13: S5.Pin_1, S5.Pin_2
  N14: S5.Pin_3, S5.Pin_4
  N15: S6.Pin_1, S6.Pin_2
  N16: S6.Pin_3, S6.Pin_4
  N17: S7.Pin_1, S7.Pin_2
  N18: S7.Pin_3, S7.Pin_4
  N19: S8.Pin_1, S8.Pin_2
  N20: S8.Pin_3, S8.Pin_4
  N21: S9.Pin_1, S9.Pin_2
  N22: S9.Pin_3, S9.Pin_4
  N23: S10.Pin_1, S10.Pin_2
  N24: S10.Pin_3, S10.Pin_4
  N25: S11.Pin_1, S11.Pin_2
  N26: S11.Pin_3, S11.Pin_4
  N27: S12.Pin_1, S12.Pin_2
  N28: S12.Pin_3, S12.Pin_4
  N29: S13.Pin_1, S13.Pin_2
  N30: S13.Pin_3, S13.Pin_4
  N31: S14.Pin_1, S14.Pin_2
  N32: S14.Pin_3, S14.Pin_4
  N33: S15.Pin_1, S15.Pin_2
  N34: S15.Pin_3, S15.Pin_4
  3V3: Arduino1.3V3, Part1.3.3V
  GND: Arduino1.GND, Part1.GND
  N35: S16.Pin_1, S16.Pin_2
  N36: S16.Pin_3, S16.Pin_4

notes:
  [encoder 1]
  [encoder 2]
  [motor controller is
  mounted on arduino]
  [3.3V !]
